// Logisim project CPU.circ as structural Verilog: 1 circuit, main circuit main
module main (
  output overflow
);

  wire adder_1_cout, adder_2_cout, and_1_out, clock_out, main_1_out_6, main_1_out_7, main_1_out_8,
       main_1_out_9, main_1_out_10, main_1_out_11, main_1_out_12, main_board_1_out_5;
  wire [3:0] multiplexer_1_out, ram_1_data_2;
  wire [11:0] ram_1_data;
  wire [15:0] adder_1_out, adder_2_out, bit_extender_1_out, bit_extender_2_out, main_board_1_final_resault,
       multiplexer_2_out, multiplexer_3_out, multiplexer_4_out, multiplexer_5_out, ram_2_data, register_1_q,
       register_file_1_data1, register_file_1_data2, shifter_1_out;

  Register #(.width(16)) register_1 (.D(multiplexer_4_out), .Q(register_1_q), .clk(clock_out));  // open: en, clr
  Clock #(.highDuration(3)) clock (.out(clock_out));
  RAM #(.addrWidth(16), .dataWidth(16)) ram_1 (
    .addr(register_1_q), .data({ram_1_data_2, ram_1_data}));  // open: sel, clk, ld, clr
  control_unit_main main_1 (
    .in_1({ram_1_data_2, 2'b00}), .out_6(main_1_out_6), .out_7(main_1_out_7), .out_8(main_1_out_8),
    .out_9(main_1_out_9), .out_10(main_1_out_10), .out_11(main_1_out_11), .out_12(main_1_out_12));  // open: in_2, function, in_4, in_5
  Multiplexer #(.width(4)) multiplexer_1 (
    .in0(ram_1_data[7:4]), .in1(ram_1_data[3:0]), .out(multiplexer_1_out), .sel(main_1_out_6));  // open: en
  Register_File register_file_1 (
    .Write_Data(multiplexer_5_out), .Data1(register_file_1_data1), .Data2(register_file_1_data2),
    .Write_Register(multiplexer_1_out), .clock(main_1_out_7), .Read_Register1(ram_1_data[7:4]),
    .Read_Register2(ram_1_data[11:8]));  // open: regWrite
  assign bit_extender_1_out = {{12{1'b0}}, ram_1_data[3:0]};  // Bit_Extender bit_extender_1
  assign bit_extender_2_out = {{12{ram_1_data[3]}}, ram_1_data[3:0]};  // Bit_Extender bit_extender_2
  Multiplexer #(.width(16)) multiplexer_2 (
    .in0(bit_extender_1_out), .in1(bit_extender_2_out), .out(multiplexer_2_out), .sel(main_1_out_12));  // open: en
  Adder #(.width(16)) adder_1 (.a(16'h1), .b(register_1_q), .out(adder_1_out), .cout(adder_1_cout));  // open: cin
  Shifter #(.width(16)) shifter_1 (.in(multiplexer_2_out), .\dist (4'b0010), .out(shifter_1_out));
  Multiplexer #(.width(16)) multiplexer_3 (
    .in0(register_file_1_data2), .in1(multiplexer_2_out), .out(multiplexer_3_out), .sel(main_1_out_10));  // open: en
  Adder #(.width(16)) adder_2 (
    .a(adder_1_out), .b(shifter_1_out), .out(adder_2_out), .cout(adder_2_cout));  // open: cin
  Multiplexer #(.width(16)) multiplexer_4 (
    .in0(adder_1_out), .in1(adder_2_out), .out(multiplexer_4_out), .sel(and_1_out));  // open: en
  and and_1 (and_1_out, main_1_out_9, main_board_1_out_5);
  Main_Board main_board_1 (
    .B(multiplexer_3_out), .A(register_file_1_data1), .Final_Resault(main_board_1_final_resault),
    .out_5(main_board_1_out_5));  // open: Operration
  RAM #(.addrWidth(16), .dataWidth(16), .bus("separate")) ram_2 (
    .addr(main_board_1_final_resault), .din(register_file_1_data2), .data(ram_2_data), .str(main_1_out_11),
    .clk(clock_out));  // open: sel, ld, clr
  Multiplexer #(.width(16)) multiplexer_5 (
    .in0(main_board_1_final_resault), .in1(ram_2_data), .out(multiplexer_5_out), .sel(main_1_out_8));  // open: en
  or or_1 (overflow, adder_2_cout, adder_1_cout);

  // Notes on the sheet:
  //   PC
endmodule
