// Logisim project alu.circ as structural Verilog
// Alu 16 bit
module Main_Board (
  input  [15:0] B,
  input  [15:0] A,
  input  [2:0] Operration,
  output [15:0] Final_Resault,
  output out_5
);

  wire subtractor_1_bout;
  wire [15:0] adder_1_out, and_1_out_3, nand_out_3, nor_1_out_3, or_1_out_3, subtractor_1_out, xnor_1_out_3,
       xor_1_out_3;

  Or or_1 (.A(A), .B(B), .out_3(or_1_out_3));
  AND and_1 (.A(A), .B(B), .out_3(and_1_out_3));
  Nand \nand  (.A(A), .B(B), .out_3(nand_out_3));
  Adder #(.width(16)) adder_1 (.a(A), .b(B), .out(adder_1_out));  // open: cin, cout
  Subtractor #(.width(16)) subtractor_1 (.a(A), .b(B), .out(subtractor_1_out), .bout(subtractor_1_bout));  // open: bin
  Nor nor_1 (.A(A), .B(B), .out_3(nor_1_out_3));
  XOR xor_1 (.A(A), .B(B), .out_3(xor_1_out_3));
  XNOR xnor_1 (.A(A), .B(B), .out_3(xnor_1_out_3));
  Comparator #(.width(16)) comparator_1 (.a(subtractor_1_out), .b({16{1'b0}}), .eq(out_5));  // open: gt, lt
  Multiplexer #(.select(3), .width(16)) multiplexer_1 (
    .in0(or_1_out_3), .in1(and_1_out_3), .in2(nand_out_3), .in3(adder_1_out), .in4(subtractor_1_out),
    .in5(nor_1_out_3), .in6(xor_1_out_3), .in7(xnor_1_out_3), .out(Final_Resault), .sel(Operration));  // open: en

  // Notes on the sheet:
  //   A: pull=up
endmodule

// OR
module Or (
  input  [15:0] A,
  input  [15:0] B,
  output [15:0] out_3
);

  assign out_3 = A | B;  // OR_Gate or_1, 16 bits wide
endmodule

module AND (
  input  [15:0] A,
  input  [15:0] B,
  output [15:0] out_3
);

  assign out_3 = A & B;  // AND_Gate and_1, 16 bits wide
endmodule

module Nand (
  input  [15:0] A,
  input  [15:0] B,
  output [15:0] out_3
);

  assign out_3 = ~(A & B);  // NAND_Gate nand_1, 16 bits wide
endmodule

module Nor (
  input  [15:0] A,
  input  [15:0] B,
  output [15:0] out_3
);

  assign out_3 = ~(A | B);  // NOR_Gate nor_1, 16 bits wide
endmodule

module XOR (
  input  [15:0] A,
  input  [15:0] B,
  output [15:0] out_3
);

  assign out_3 = A ^ B;  // XOR_Gate xor_1, 16 bits wide
endmodule

module XNOR (
  input  [15:0] A,
  input  [15:0] B,
  output [15:0] out_3
);

  assign out_3 = ~(A ^ B);  // XNOR_Gate xnor_1, 16 bits wide
endmodule

module Alu_16_bit (
  input  [15:0] in_1,
  input  [15:0] in_2,
  input  [2:0] in_3,
  output [15:0] out_4
);

  Main_Board main_board_1 (.B(in_2), .A(in_1), .Operration(in_3), .Final_Resault(out_4));  // open: out_5
endmodule
