// Logisim project control_unit.circ as structural Verilog: 1 circuit, main circuit main
module main (
  input  [5:0] in_1,
  input  [2:0] in_2,
  input  \function ,
  input  in_4,
  input  in_5,
  output out_6,
  output out_7,
  output out_8,
  output out_9,
  output out_10,
  output out_11,
  output out_12
);

  wire addi_out, not_1_out, not_2_out, not_3_out, not_4_out, not_5_out, not_6_out, not_7_out, not_9_out,
       not_10_out, not_11_out, not_12_out, not_13_out, not_14_out, not_15_out, not_16_out, not_17_out,
       not_18_out, not_19_out, not_20_out, not_21_out, not_22_out, not_23_out, not_24_out, not_25_out,
       not_26_out, not_27_out, not_28_out, not_29_out;
  wire [2:0] multiplexer_1_out, undriven;
  wire [2:2] ori_out;

  not not_1 (not_1_out, in_1[0]);
  not not_2 (not_2_out, in_1[1]);
  not not_3 (not_3_out, in_1[2]);
  not not_4 (not_4_out, in_1[3]);
  not not_5 (not_5_out, in_1[4]);
  not not_6 (not_6_out, in_1[5]);
  not not_7 (not_7_out, in_1[1]);
  not not_8 (not_7_out, in_1[2]);
  not not_9 (not_9_out, in_1[3]);
  not not_10 (not_10_out, in_1[4]);
  not not_11 (not_11_out, in_1[5]);
  not not_12 (not_12_out, in_1[0]);
  not not_13 (not_13_out, in_1[2]);
  not not_14 (not_14_out, in_1[3]);
  not not_15 (not_15_out, in_1[4]);
  not not_16 (not_16_out, in_1[5]);
  not not_17 (not_17_out, in_1[2]);
  not not_18 (not_18_out, in_1[3]);
  not not_19 (not_19_out, in_1[4]);
  not not_20 (not_20_out, in_1[5]);
  not not_21 (not_21_out, in_1[0]);
  not not_22 (not_22_out, in_1[1]);
  not not_23 (not_23_out, in_1[3]);
  not not_24 (not_24_out, in_1[4]);
  not not_25 (not_25_out, in_1[5]);
  not not_26 (not_26_out, in_1[1]);
  not not_27 (not_27_out, in_1[3]);
  not not_28 (not_28_out, in_1[4]);
  not not_29 (not_29_out, in_1[5]);
  and R_type (out_6, not_1_out, not_2_out, not_3_out, not_4_out, not_5_out, not_6_out);
  and beq (out_9, in_1[0], not_7_out, not_7_out, not_9_out, not_10_out, not_11_out);
  and lw (out_8, not_12_out, in_1[1], not_13_out, not_14_out, not_15_out, not_16_out);
  and sw (out_11, in_1[0], in_1[1], not_17_out, not_18_out, not_19_out, not_20_out);
  and addi (addi_out, not_21_out, not_22_out, in_1[2], not_23_out, not_24_out, not_25_out);
  and ori (ori_out[2], in_1[0], not_26_out, in_1[2], not_27_out, not_28_out, not_29_out);
  or register_write (out_7, out_6, out_8, addi_out, ori_out[2]);
  or alu_src (out_10, out_8, out_11, addi_out, ori_out[2]);
  or ExtOp (out_12, out_11, addi_out);
  Multiplexer #(.width(3)) multiplexer_1 (
    .in0({ori_out[2], out_9, out_6}), .in1(undriven), .out(multiplexer_1_out), .sel(out_6));  // open: en

  // Notes on the sheet:
  //   mem to reg
  //   mem to write
  //   Reg destination
  //   branch
  //   alu control
endmodule
